# Fritzing sketch box1 (saved by Fritzing 0.9.2b)
breadboards: 1

parts:
  Componente1 = Arduino Leonardo (Rev3b)
  LED1 = LED - 5mm [color="Red (633nm)" package="5 mm [THT]"]
  LED2 = LED - 5mm [color="Yellow (595nm)" package="5 mm [THT]"]
  LED3 = LED - 5mm [color="Green (570nm)" package="5 mm [THT]"]
  R1 = Resistor [tolerance=±5% resistance=220 package=THT]
  R2 = Resistor [tolerance=±5% resistance=220 package=THT]
  R3 = Resistor [tolerance=±5% resistance=220 package=THT]
  C1 = Ceramic Capacitor [capacitance=100nF package="100 mil [THT, multilayer]"]
  J1 = Basic Servo
  R4 = Photocell (LDR) [package=THT]
  R5 = Resistor [tolerance=±5% resistance=1M package=THT]
  R6 = Resistor [tolerance=±5% resistance=220 package=THT]
  J2 = Piezo Speaker

nets:
  N1: Componente1.D3_PWM/SCL, R1.Pin_1
  N2: Componente1.D4/A6, R2.Pin_1
  N3: Componente1.D5_PWM, R3.Pin_1
  N4: Componente1.5V, R4.pin_1, J2.pin2
  GND: Componente1.GND, LED1.cathode, LED2.cathode, LED3.cathode, C1.0, C1.1, J1.gnd, R5.Pin_1, R6.Pin_0
  N5: Componente1.A0, R5.Pin_0, J2.pin1
  N6: Componente1.A5, R4.pin_0, R6.Pin_1
  N7: Componente1.D9_PWM/A9, J1.pulse
  N8: LED1.anode, R3.Pin_0
  N9: LED2.anode, R1.Pin_0
  N10: LED3.anode, R2.Pin_0
