# Fritzing sketch secondo_def (saved by Fritzing 0.9.2b)
breadboards: 1

parts:
  Componente1 = Arduino Leonardo (Rev3b)
  J1 = Piezo Speaker
  J2 = Basic Servo
  LED1 = RGB LED - (4 legs) [package="5 mm [THT]"]
  R1 = Resistor [tolerance=±5% resistance=220 package=THT]
  R2 = Resistor [tolerance=±5% resistance=220 package=THT]
  R3 = PHOTOCELL [package=photocell-kit]
  R6 = Resistor [tolerance=±5% resistance=1M package=THT]
  C2 = Ceramic Capacitor [capacitance=100nF package="100 mil [THT, multilayer]"]
  R7 = Resistor [tolerance=±5% resistance=220 package=THT]
  R8 = Resistor [tolerance=±5% resistance=220 package=THT]

nets:
  N1: Componente1.D3_PWM/SCL, R2.Pin_1
  N2: Componente1.D4/A6, R8.Pin_1
  N3: Componente1.D5_PWM, R7.Pin_1
  5V: Componente1.5V, J2.vcc
  GND: Componente1.GND, J2.gnd
  N4: Componente1.A0, J1.pin1, R6.Pin_1
  N5: Componente1.A5, R1.Pin_1, R3.P$2
  N6: J1.pin2, LED1.green_cathode, R1.Pin_0, R3.P$1, R6.Pin_0, C2.0, C2.1
