# Fritzing sketch Circuito leonardo ventole (saved by Fritzing 0.9.2b)
breadboards: 1

parts:
  Componente1 = Arduino Leonardo (Rev3b)
  Q2 = Basic FET P-Channel [package="TO220 [THT]"]
  M1 = DC Motor
  D1 = Diode [package=diode-1n4001]

nets:
  N1: Componente1.D3_PWM/SCL, Q2.gate
  N2: Q2.drain, M1.pin_2, D1.A

notes:
  12V
